# Fritzing sketch wiring (saved by Fritzing 0.9.3b)
circuit board: 6.86125cm x 2.7937cm

parts:
  Raspberry_Pi1 = Raspberry Pi 2
  Part1 = Thermal Printer with DTR
  U2 = Luxeon LED [package=luxeon]
  U3 = Luxeon LED [package=luxeon]
  S1 = Round Pushbutton [part_number=led_push]
  D1 = LTE-302 [package=lte-302]
  R1 = Resistor [tolerance=±5% resistance=2 package=THT]
  R2 = Resistor [tolerance=±5% resistance=2 package=THT]
  J2_-_5V = Power plug
  J1_-_9V = Power plug
  R3 = Resistor [tolerance=±5% resistance=1k package=THT]
  Q1 = NPN-Transistor [part_number=BC547A package="TO92 [THT]"]
  Q2 = MOSFET-NCHANNEL [part_number=IRFZ44N package=to220v]
  R4 = Resistor [tolerance=±5% resistance=2.2k package=THT]
  U4 = G3VM-61E1 [part_number=relay package=g3vm-61e1]

nets:
  GND: Raspberry_Pi1.GND, Part1.GND, S1.leg1, D1.C, J2_-_5V.GND, J1_-_9V.GND, Q1.E, Q2.S, U4.P$6
  N1: Raspberry_Pi1.GPIO27, U4.P$4
  N2: Raspberry_Pi1.GPIO13, R3.Pin_0
  N3: Raspberry_Pi1.GPIO16, Part1.DTR
  N4: Raspberry_Pi1.GPIO23, S1.leg0
  N5: Raspberry_Pi1.GPIO18, D1.A
  N6: Raspberry_Pi1.GPIO15, Part1.TXD
  N7: Raspberry_Pi1.GPIO14, Part1.RXD
  N8: Raspberry_Pi1.5V, U4.P$5
  N9: Part1.VH, J1_-_9V.VCC, R4.Pin_1
  N10: U2.A, U3.A, J2_-_5V.VCC
  N11: U2.C, R1.Pin_1
  N12: U3.C, R2.Pin_1
  N13: R1.Pin_0, R2.Pin_0, Q2.D
  N14: R3.Pin_1, Q1.B
  N15: Q1.C, Q2.G, R4.Pin_0

custom parts:
  Thermal Printer with DTR: Description: This is a thermal printer like you would find on a cash register or adding machine. It will print simple strings passed to it via TTL serial, bitmap images (poorly) and it even generates several different formats of barcodes! The thermal printer takes 2.25" (57mm) wide thermal paper with a max roll diameter of 1.5" (39mm). Thermal paper is inexpensive and commonly found in most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
